// Digital circuit 1-bit-memory.dig as structural Verilog
module _1_bit_memory (
  input  InputBit,
  input  Read_Write,
  input  Operate,
  output OutputBit
);

  wire and_1_out, and_2_out, d_ff_1_q;

  and and_1 (and_1_out, Operate, InputBit);
  and and_2 (and_2_out, Read_Write, Operate);
  D_FF d_ff_1 (.D(and_1_out), .C(and_2_out), .Q(d_ff_1_q));  // open: nQ
  and and_3 (OutputBit, d_ff_1_q, Operate);
endmodule
